// Logisim project TinyCPU.circ as structural Verilog: 6 circuits, main circuit TinyCPU
module TinyCPU (
  input  CLK,
  output HALTED
);

  wire errorflags_1_ovf_out;
  wire [11:0] addresspath_1_address;
  wire [15:0] datapath_1_acc_out, memory_1_data_out;

  // FetchDecode fetchdecode_1: pin names not known; wires that end beside it: CLK, CLK
  Datapath datapath_1 (.ACC_OUT(datapath_1_acc_out));  // open: DATA_IN, ACC_LOAD, VALID_IN, CLK, ACC_VALID_OUT, ZERO, NEGATIVE
  AddressPath addresspath_1 (.ADDRESS(addresspath_1_address));  // open: ADDRESS_IN, OFFSET, AR_LOAD, VALID_IN, CLK, ADDRESS_VALID, ADDRESS_PLUS_OFFSET, OFFSET_CARRY
  Memory memory_1 (.DATA_OUT(memory_1_data_out));  // open: ADDRESS, DATA_IN, VALID_IN, WRITE_ENABLE, CLK, VALID_OUT
  ErrorFlags errorflags_1 (.OVF_OUT(errorflags_1_ovf_out));  // open: CLEAR_ERROR, CLK, SET_OVF, SET_DIV0, SET_ADDR, SET_INV, SET_ILL, SET_INPUT, DIV0_OUT, ADDR_OUT, INV_OUT, ILL_OUT, INPUT_OUT

  // Notes on the sheet:
  //   TinyCPU AP 5: countdown fixture and clock-edge trace boundary
endmodule

module FetchDecode (
  input  CLK,
  input  RESET,
  input  ZERO,
  input  [11:0] PROGRAM_LIMIT,
  input  NEGATIVE,
  input  ERROR,
  output [15:0] OPERAND,
  output LOAD_CONST,
  output STORE_ADDRESS,
  output ADD_ADDRESS,
  output JUMP_NOT_ZERO,
  output PRINT,
  output HALT,
  output SET_ADDR,
  output HALT_ERROR,
  output [11:0] PC_OUT,
  output LOAD_ADDRESS,
  output LOAD_ADDRESS_REGISTER,
  output LOAD_ADDRESS_REGISTER_PLUS_OFFSET,
  output ADD_CONST,
  output ADD_ADDRESS_REGISTER,
  output ADD_ADDRESS_REGISTER_PLUS_OFFSET,
  output SUB_CONST,
  output SUB_ADDRESS,
  output SUB_ADDRESS_REGISTER,
  output SUB_ADDRESS_REGISTER_PLUS_OFFSET,
  output MUL_CONST,
  output MUL_ADDRESS,
  output MUL_ADDRESS_REGISTER,
  output MUL_ADDRESS_REGISTER_PLUS_OFFSET,
  output DIV_CONST,
  output DIV_ADDRESS,
  output DIV_ADDRESS_REGISTER,
  output DIV_ADDRESS_REGISTER_PLUS_OFFSET,
  output AND_CONST,
  output AND_ADDRESS,
  output AND_ADDRESS_REGISTER,
  output AND_ADDRESS_REGISTER_PLUS_OFFSET,
  output OR_CONST,
  output OR_ADDRESS,
  output OR_ADDRESS_REGISTER,
  output OR_ADDRESS_REGISTER_PLUS_OFFSET,
  output STORE_ADDRESS_REGISTER,
  output STORE_ADDRESS_REGISTER_PLUS_OFFSET,
  output LOAD_ADDRESS_REGISTER_CONST,
  output LOAD_ADDRESS_REGISTER_ADDRESS,
  output NOT,
  output JUMP_ADDRESS,
  output JUMP_ZERO,
  output JUMP_NEGATIVE,
  output JUMP_ERROR,
  output JUMP_NOT_ERROR,
  output CLEAR_ERROR,
  output INPUT,
  output PRINT_ADDRESS,
  output SET_OVF,
  output SET_DIV0,
  output SET_INV,
  output SET_ILL,
  output SET_INPUT
);

  wire [10:5] PC_INCREMENT_p1;

  Register #(.width(12)) PC ();  // open: D, en, clk, Q, clr
  // Adder #(.width(12)) PC_INCREMENT: pin names not known; wires that end beside it: {PC_INCREMENT_p1, OPERAND[15:12], PROGRAM_LIMIT[11:1], CLK}, {PC_INCREMENT_p1, OPERAND[15:12], PROGRAM_LIMIT[11:1], CLK}
  Multiplexer #(.select(1), .width(12)) PC_SOURCE (.out({PROGRAM_LIMIT[11:1], CLK}));  // open: in0, in1, sel
  ROM #(.addrWidth(12), .dataWidth(22)) INSTRUCTION_ROM (
    .addr({PROGRAM_LIMIT[11:1], CLK}), .data({PC_INCREMENT_p1, OPERAND[15:12], PROGRAM_LIMIT[11:1], CLK}));
  Comparator #(.width(12)) PC_RANGE (
    .a({PROGRAM_LIMIT[11:1], CLK}), .b({PROGRAM_LIMIT[11:1], CLK}), .eq(CLK));  // open: gt, lt
  // Decoder #(.select(6)) ISA_DECODER: pin names not known; wires that end beside it: {PC_INCREMENT_p1, OPERAND[15:12], PROGRAM_LIMIT[11:1], CLK}
  // AND_Gate JNZ_TAKEN has open pins: out=CLK
  // OR_Gate ERROR_HALT has open pins: out=CLK
  // Pins of 1 and 12 and 16 and 22 bits meet at {PC_INCREMENT_p1, OPERAND[15:12], PROGRAM_LIMIT[11:1], CLK}

  assign ADD_ADDRESS = CLK;
  assign HALT = CLK;
  assign HALT_ERROR = CLK;
  assign JUMP_NOT_ZERO = CLK;
  assign LOAD_CONST = CLK;
  assign OPERAND[11:0] = {PROGRAM_LIMIT[11:1], CLK};
  assign PC_OUT = {PROGRAM_LIMIT[11:1], CLK};
  assign PRINT = CLK;
  assign PROGRAM_LIMIT[0] = CLK;
  assign RESET = CLK;
  assign SET_ADDR = CLK;
  assign STORE_ADDRESS = CLK;

  // Notes on the sheet:
  //   AP 7 machine format v1: stable six-bit opcode allocation and encoder-generated ROM
  //   contents of INSTRUCTION_ROM (hex, n*v repeats v):
  //   00ffff 1c0065 000003 1c0064 2a0000 050065 1c0064 240004 2c0000
endmodule

module Datapath (
  input  [15:0] DATA_IN,
  input  ACC_LOAD,
  input  VALID_IN,
  input  CLK,
  output [15:0] ACC_OUT,
  output ACC_VALID_OUT,
  output ZERO,
  output NEGATIVE
);

  Register #(.width(16)) ACC (.D(DATA_IN), .Q(ACC_OUT), .clk(ACC_LOAD));  // open: en, clr
  // Register #(.width(1)) ACC_VALID: pin names not known; wires that end beside it: CLK, ACC_LOAD, ACC_VALID_OUT
  Comparator #(.mode("twosComplement"), .width(16)) ACC_STATUS (
    .a(ACC_OUT), .b({16{1'b0}}), .eq(ZERO), .lt(NEGATIVE));  // open: gt

  assign VALID_IN = CLK;

  // Notes on the sheet:
  //   Clocked 16-bit accumulator; signed comparator derives ZERO and NEGATIVE
endmodule

module AddressPath (
  input  [11:0] ADDRESS_IN,
  input  [11:0] OFFSET,
  input  AR_LOAD,
  input  VALID_IN,
  input  CLK,
  output [11:0] ADDRESS,
  output ADDRESS_VALID,
  output [11:0] ADDRESS_PLUS_OFFSET,
  output OFFSET_CARRY
);

  Register #(.width(12)) AR (.D(ADDRESS_IN), .Q(OFFSET), .clk(AR_LOAD));  // open: en, clr
  // Register #(.width(1)) AR_VALID: pin names not known; wires that end beside it: VALID_IN, ADDRESS_VALID, OFFSET
  // Adder #(.width(12)) OFFSET_ADDER: pin names not known; wires that end beside it: OFFSET, ADDRESS_PLUS_OFFSET, OFFSET_CARRY

  assign ADDRESS = OFFSET;

  // Notes on the sheet:
  //   Clocked 12-bit address register with combinational offset addition
endmodule

module Memory (
  input  [11:0] ADDRESS,
  input  [15:0] DATA_IN,
  input  VALID_IN,
  input  WRITE_ENABLE,
  input  CLK,
  output [15:0] DATA_OUT,
  output VALID_OUT
);

  wire DATA_RAM_p2, DATA_RAM_p3, DATA_RAM_p10;

  // RAM #(.addrWidth(12), .dataWidth(16)) DATA_RAM: pin names not known; wires that end beside it: DATA_IN, DATA_RAM_p2, DATA_RAM_p3, ADDRESS, VALID_IN, DATA_RAM_p2, DATA_RAM_p3, DATA_OUT, VALID_OUT, DATA_RAM_p10
  // RAM #(.addrWidth(12), .dataWidth(1)) VALID_RAM: pin names not known; wires that end beside it: VALID_IN, DATA_RAM_p2, DATA_RAM_p3, VALID_OUT, DATA_RAM_p10

  // Notes on the sheet:
  //   4096-word value/valid memory with shared address, write-enable, and clock
endmodule

module ErrorFlags (
  input  CLEAR_ERROR,
  input  CLK,
  input  SET_OVF,
  input  SET_DIV0,
  input  SET_ADDR,
  input  SET_INV,
  input  SET_ILL,
  input  SET_INPUT,
  output OVF_OUT,
  output DIV0_OUT,
  output ADDR_OUT,
  output INV_OUT,
  output ILL_OUT,
  output INPUT_OUT
);

  wire HOLD_ADDR_out, HOLD_DIV0_out, HOLD_ILL_out, HOLD_INPUT_out, HOLD_INV_out, HOLD_OVF_out,
       NOT_CLEAR_ERROR_out;

  not NOT_CLEAR_ERROR (NOT_CLEAR_ERROR_out, CLEAR_ERROR);
  and HOLD_OVF (HOLD_OVF_out, OVF_OUT, NOT_CLEAR_ERROR_out);
  and HOLD_DIV0 (HOLD_DIV0_out, DIV0_OUT, NOT_CLEAR_ERROR_out);
  and HOLD_ADDR (HOLD_ADDR_out, ADDR_OUT, NOT_CLEAR_ERROR_out);
  and HOLD_INV (HOLD_INV_out, INV_OUT, NOT_CLEAR_ERROR_out);
  and HOLD_ILL (HOLD_ILL_out, ILL_OUT, NOT_CLEAR_ERROR_out);
  and HOLD_INPUT (HOLD_INPUT_out, INPUT_OUT, NOT_CLEAR_ERROR_out);
  or NEXT_OVF (CLK, SET_OVF, HOLD_OVF_out);
  or NEXT_DIV0 (CLK, SET_DIV0, HOLD_DIV0_out);
  or NEXT_ADDR (CLK, SET_ADDR, HOLD_ADDR_out);
  or NEXT_INV (CLK, SET_INV, HOLD_INV_out);
  or NEXT_ILL (CLK, SET_ILL, HOLD_ILL_out);
  or NEXT_INPUT (CLK, SET_INPUT, HOLD_INPUT_out);
  // Register #(.width(1)) OVF: pin names not known; wires that end beside it: OVF_OUT, DIV0_OUT
  // Register #(.width(1)) DIV0: pin names not known; wires that end beside it: DIV0_OUT, ADDR_OUT
  // Register #(.width(1)) ADDR: pin names not known; wires that end beside it: ADDR_OUT, INV_OUT
  // Register #(.width(1)) INV: pin names not known; wires that end beside it: INV_OUT, ILL_OUT
  // Register #(.width(1)) ILL: pin names not known; wires that end beside it: CLK, ILL_OUT, INPUT_OUT
  // Register #(.width(1)) INPUT: pin names not known; wires that end beside it: CLK, INPUT_OUT

  // Notes on the sheet:
  //   Set-dominant sticky flags: SET OR (current AND NOT CLEAR_ERROR)
endmodule
