// Logisim project TinyCPU-AddressPath.circ as structural Verilog: 1 circuit, main circuit AddressPath
module AddressPath (
  input  [11:0] ADDRESS_IN,
  input  AR_LOAD,
  input  [11:0] OFFSET,
  input  VALID_IN,
  input  CLK,
  output [11:0] ADDRESS,
  output [11:0] ADDRESS_PLUS_OFFSET,
  output OFFSET_CARRY,
  output ADDRESS_VALID
);

  // Register #(.width(12)) AR: pin names not known; wires that end beside it: ADDRESS_IN, AR_LOAD, CLK, ADDRESS
  // Register #(.width(1)) AR_VALID: pin names not known; wires that end beside it: VALID_IN, AR_LOAD, CLK, ADDRESS_VALID
  Adder #(.width(12)) OFFSET_ADDER (.out(ADDRESS_PLUS_OFFSET), .cout(OFFSET_CARRY));  // open: a, b, cin

  // Notes on the sheet:
  //   Clocked 12-bit address register with combinational offset addition
endmodule
