// Logisim project TinyCPU-FetchDecode.circ as structural Verilog: 1 circuit, main circuit FetchDecode
module FetchDecode (
  input  CLK,
  input  RESET,
  input  ZERO,
  input  [11:0] PROGRAM_LIMIT,
  input  NEGATIVE,
  input  ERROR,
  output [15:0] OPERAND,
  output LOAD_CONST,
  output STORE_ADDRESS,
  output ADD_ADDRESS,
  output JUMP_NOT_ZERO,
  output PRINT,
  output HALT,
  output SET_ADDR,
  output HALT_ERROR,
  output [11:0] PC_OUT,
  output LOAD_ADDRESS,
  output LOAD_ADDRESS_REGISTER,
  output LOAD_ADDRESS_REGISTER_PLUS_OFFSET,
  output ADD_CONST,
  output ADD_ADDRESS_REGISTER,
  output ADD_ADDRESS_REGISTER_PLUS_OFFSET,
  output SUB_CONST,
  output SUB_ADDRESS,
  output SUB_ADDRESS_REGISTER,
  output SUB_ADDRESS_REGISTER_PLUS_OFFSET,
  output MUL_CONST,
  output MUL_ADDRESS,
  output MUL_ADDRESS_REGISTER,
  output MUL_ADDRESS_REGISTER_PLUS_OFFSET,
  output DIV_CONST,
  output DIV_ADDRESS,
  output DIV_ADDRESS_REGISTER,
  output DIV_ADDRESS_REGISTER_PLUS_OFFSET,
  output AND_CONST,
  output AND_ADDRESS,
  output AND_ADDRESS_REGISTER,
  output AND_ADDRESS_REGISTER_PLUS_OFFSET,
  output OR_CONST,
  output OR_ADDRESS,
  output OR_ADDRESS_REGISTER,
  output OR_ADDRESS_REGISTER_PLUS_OFFSET,
  output STORE_ADDRESS_REGISTER,
  output STORE_ADDRESS_REGISTER_PLUS_OFFSET,
  output LOAD_ADDRESS_REGISTER_CONST,
  output LOAD_ADDRESS_REGISTER_ADDRESS,
  output NOT,
  output JUMP_ADDRESS,
  output JUMP_ZERO,
  output JUMP_NEGATIVE,
  output JUMP_ERROR,
  output JUMP_NOT_ERROR,
  output CLEAR_ERROR,
  output INPUT,
  output PRINT_ADDRESS,
  output SET_OVF,
  output SET_DIV0,
  output SET_INV,
  output SET_ILL,
  output SET_INPUT
);

  wire PC_INCREMENT_p2, PC_p1, PC_SOURCE_p2;
  wire [21:16] INSTRUCTION_ROM_data;

  // Register #(.width(12)) PC: pin names not known; wires that end beside it: PC_p1, CLK, RESET
  // Adder #(.width(12)) PC_INCREMENT: pin names not known; wires that end beside it: PC_OUT, PC_INCREMENT_p2
  // Multiplexer #(.select(1), .width(12)) PC_SOURCE: pin names not known; wires that end beside it: PC_INCREMENT_p2, PC_SOURCE_p2, PC_p1
  ROM #(.addrWidth(12), .dataWidth(22)) INSTRUCTION_ROM (.addr(PC_OUT), .data({INSTRUCTION_ROM_data, OPERAND}));
  Comparator #(.width(12)) PC_RANGE (.a(PC_OUT), .b(PROGRAM_LIMIT), .eq(HALT));  // open: gt, lt
  // Decoder #(.select(6)) ISA_DECODER: pin names not known; wires that end beside it: {INSTRUCTION_ROM_data, OPERAND}, LOAD_CONST, STORE_ADDRESS, ADD_ADDRESS, JUMP_NOT_ZERO
  // AND_Gate JNZ_TAKEN has open pins: out=PC_SOURCE_p2
  // OR_Gate ERROR_HALT has open pins: out=HALT
  // Pins of 16 and 22 bits meet at {INSTRUCTION_ROM_data, OPERAND}

  assign HALT_ERROR = HALT;
  assign SET_ADDR = HALT;

  // Notes on the sheet:
  //   AP 7 machine format v1: stable six-bit opcode allocation and encoder-generated ROM
  //   contents of INSTRUCTION_ROM (hex, n*v repeats v):
  //   00ffff 1c0065 000003 1c0064 2a0000 050065 1c0064 240004 2c0000
endmodule
